// Logisim project CPU-2014-Proj.circ as structural Verilog
module main (
);

  wire [15:0] Instruction_Register_q, ram_1_data;

  Register_part #(.width(16)) Instruction_Register (.D(ram_1_data), .Q(Instruction_Register_q));  // open: en, clk, clr
  ALU ALU ();  // open: in_1, in_2, OP, IMM, out_5
  // Decoder Decoder: pin names not known; wires that end beside it: Instruction_Register_q
  RAM #(.dataWidth(16)) ram_1 (.data(ram_1_data));  // open: addr, sel, clk, ld, clr
endmodule

module ALU (
  input  [7:0] in_1,
  input  [7:0] in_2,
  input  [1:0] OP,
  input  [7:0] IMM,
  output [7:0] out_5
);

  wire [7:0] adder_1_out, and_1_out, or_1_out, subtractor_1_out, undriven;

  assign and_1_out = in_1 & in_2 & undriven;  // AND_Gate and_1, 8 bits wide
  assign or_1_out = undriven | in_1 | in_2;  // OR_Gate or_1, 8 bits wide
  Adder adder_1 (.a(in_1), .b(in_2), .out(adder_1_out));  // open: cin, cout
  Subtractor subtractor_1 (.a(in_1), .b(in_2), .out(subtractor_1_out));  // open: bin, bout
  Multiplexer #(.select(2), .width(8), .enable("false")) multiplexer_1 (
    .in0(and_1_out), .in1(or_1_out), .in2(adder_1_out), .in3(subtractor_1_out), .out(out_5), .sel(OP));
endmodule

module Decoder (
  input  [7:0] irvalue,
  output [1:0] phase,
  output [1:0] dregsel,
  output [1:0] sregsel,
  output [1:0] aluop,
  output imload,
  output imload_2,
  output irload
);

  wire and_1_out, clock_1_out, undriven;
  wire [1:0] phase_t;

  Multiplexer #(.select(2), .enable("false")) multiplexer_1 (
    .in0(1'b1), .in1(1'b0), .in2(1'b0), .in3(1'b0), .out(irload), .sel(phase_t));
  Multiplexer #(.select(2), .enable("false")) multiplexer_2 (
    .in0(1'b0), .in1(irvalue[7]), .in2(1'b0), .in3(1'b0), .out(imload), .sel(phase_t));
  Clock clock_1 (.out(clock_1_out));
  Register_part #(.width(2)) register_1 (.Q(phase), .clk(clock_1_out), .clr(and_1_out));  // open: D, en
  and and_1 (and_1_out, phase[0], phase[1]);
  Multiplexer #(.select(2), .enable("false")) multiplexer_3 (
    .in0(1'b1), .in1(irvalue[7]), .in2(undriven), .in3(1'b0), .out(imload_2), .sel(phase_t));

  assign aluop = {irvalue[7], irvalue[4]};
  assign dregsel = irvalue[3:2];
  assign {irvalue[6:5], irvalue[0]} = {3{irvalue[7]}};
  assign sregsel = {irvalue[1], irvalue[7]};

  // Other names for the same wires on the sheet: irbit5 = irvalue[7]; irbit6 = irvalue[7]; irbit7 = irvalue[7];
  //   op1[1:0] = {2{irvalue[7]}}; op1op2[3:0] = {irvalue[4], {3{irvalue[7]}}}; op2[1:0] = {irvalue[7], irvalue[4]};
  //   Rs[1:0] = {irvalue[1], irvalue[7]}; irbit4 = irvalue[4]; Rd[1:0] = irvalue[3:2]

  // Notes on the sheet:
  //   IR Load
  //   Decode Logic
  //   Immediate Load
  //   Phase Counter
  //   PC Load
endmodule
